# Fritzing sketch 01 (saved by Fritzing 0.9.3b)

parts:
  Part2 = SwiftIO
  Grove3 = Grove Infrared Emitter
  Grove4 = Grove Rotary Angle Sensor

nets:
  N1: Part2.A6~, Grove4.SIG
  N2: Part2.A7~, Grove4.NC
  N3: Part2.3V3#86, Grove4.VCC
  N4: Part2.GND#87, Grove4.GND
  N5: Part2.D10~, Grove3.TX
  N6: Part2.3V3#102, Grove3.VCC
  N7: Part2.GND#103, Grove3.GND

custom parts:
  SwiftIO: SwiftIO offers a full Swift compiler and framework environment that runs on the microcontroller. The SwiftIO board is a compact electronic circuit board that runs Swift on the bare metal, giving you a system that can be used to control all kinds of electronic projects.
  Grove Rotary Angle Sensor: A potentiometer
