# Fritzing sketch 02 (saved by Fritzing 0.9.3b)
breadboards: 1

parts:
  Part2 = SwiftIO
  RE1 = Rotary Encoder [package=THT]
  LED1 = LED - 5mm [color="Red (633nm)" package="5 mm [THT]"]

nets:
  N1: Part2.GND#0, RE1.EncoderPinB
  N2: Part2.3V3, RE1.EncoderPinA
  N3: Part2.P20/D20/A6, RE1.EncoderPinC
  N4: Part2.GND#35, LED1.cathode
  N5: Part2.P10/D10/PWM2B, LED1.anode

custom parts:
  SwiftIO: SwiftIO offers a full Swift compiler and framework environment that runs on the microcontroller. The SwiftIO board is a compact electronic circuit board that runs Swift on the bare metal, giving you a system that can be used to control all kinds of electronic projects.
