# Fritzing sketch 03 (saved by Fritzing 0.9.3b)

parts:
  RE1 = Rotary Encoder [package=THT]
  LED1 = LED - 5mm [color="Red (633nm)" package="5 mm [THT]"]
  Part1 = SwiftIO
  R1 = Resistor [tolerance=±5% resistance=220 package=THT]

nets:
  N1: RE1.EncoderPinA, Part1.3V3
  N2: RE1.EncoderPinC, Part1.P20/D20/A6
  N3: RE1.EncoderPinB, Part1.GND#0
  N4: LED1.cathode, R1.Pin_1
  N5: LED1.anode, Part1.P10/D10/PWM2B
  N6: Part1.GND#35, R1.Pin_0

custom parts:
  SwiftIO: SwiftIO offers a full Swift compiler and framework environment that runs on the microcontroller. The SwiftIO board is a compact electronic circuit board that runs Swift on the bare metal, giving you a system that can be used to control all kinds of electronic projects.
