# Fritzing sketch BrightnessAnalogIn (saved by Fritzing 0.9.3b)
breadboards: 1

parts:
  元件1 = SwiftIO
  元件2 = SwiftIO  # not connected
  LED1 = LED - 5mm [color="Red (633nm)" package="5 mm [THT]"]
  R1 = Rotary Potentiometer (Small) [maximum_resistance=100kΩ package=THT]
  R2 = Resistor [tolerance=±5% resistance=220 package=THT]

nets:
  N1: 元件1.P20/D20/A6, R1.wiper
  N2: 元件1.GND#35, R2.Pin_0
  N3: 元件1.3V3, R1.leg1
  N4: 元件1.P10/D10/PWM2B, LED1.anode
  N5: 元件1.GND#70, R1.leg2
  N6: LED1.cathode, R2.Pin_1

custom parts:
  SwiftIO: SwiftIO offers a full Swift compiler and framework environment that runs on the microcontroller. The SwiftIO board is a compact electronic circuit board that runs Swift on the bare metal, giving you a system that can be used to control all kinds of electronic projects.
  SwiftIO: SwiftIO offers a full Swift compiler and framework environment that runs on the microcontroller. The SwiftIO board is a compact electronic circuit board that runs Swift on the bare metal, giving you a system that can be used to control all kinds of electronic projects.
