# Fritzing sketch ButtoncontrolLED (saved by Fritzing 0.9.3b)
breadboards: 1

parts:
  S1 = Pushbutton [package="[THT]"]
  元件1 = SwiftIO

nets:
  N1: S1.Pin_1, S1.Pin_2, 元件1.P0/D0/UART0_RX
  N2: S1.Pin_3, S1.Pin_4, 元件1.3V3

custom parts:
  SwiftIO: SwiftIO offers a full Swift compiler and framework environment that runs on the microcontroller. The SwiftIO board is a compact electronic circuit board that runs Swift on the bare metal, giving you a system that can be used to control all kinds of electronic projects.
