# Fritzing sketch LEDsBrightness (saved by Fritzing 0.9.3b)
breadboards: 1

parts:
  LED7 = LED - 5mm [color="Blue (525nm)" package="5 mm [THT]"]
  LED8 = LED - 5mm [color="Green (560nm)" package="5 mm [THT]"]
  LED9 = LED - 5mm [color="Red (633nm)" package="5 mm [THT]"]
  R1 = Resistor [tolerance=±5% resistance=220 package=THT]
  R2 = Resistor [tolerance=±5% resistance=220 package=THT]
  R3 = Resistor [tolerance=±5% resistance=220 package=THT]
  元件2 = SwiftIO
  元件3 = SwiftIO  # not connected

nets:
  N1: LED7.cathode, R1.Pin_1
  N2: LED7.anode, 元件2.P44/D44
  N3: LED8.cathode, R2.Pin_1
  N4: LED8.anode, 元件2.P12/D12/PWM3B/UART_RX
  N5: LED9.cathode, R3.Pin_1
  N6: LED9.anode, 元件2.P10/D10/PWM2B
  N7: R1.Pin_0, R2.Pin_0, R3.Pin_0, 元件2.GND

custom parts:
  SwiftIO: SwiftIO offers a full Swift compiler and framework environment that runs on the microcontroller. The SwiftIO board is a compact electronic circuit board that runs Swift on the bare metal, giving you a system that can be used to control all kinds of electronic projects.
  SwiftIO: SwiftIO offers a full Swift compiler and framework environment that runs on the microcontroller. The SwiftIO board is a compact electronic circuit board that runs Swift on the bare metal, giving you a system that can be used to control all kinds of electronic projects.
