# Fritzing sketch PWMBrightnessControl (saved by Fritzing 0.9.3b)
breadboards: 1

parts:
  元件1 = SwiftIO  # not connected
  元件2 = SwiftIO
  R1 = Resistor [tolerance=±5% resistance=220 package=THT]
  LED1 = LED - 5mm [color="Red (633nm)" package="5 mm [THT]"]

nets:
  N1: 元件2.GND, R1.Pin_0
  N2: 元件2.P10/D10/PWM2B, LED1.anode
  N3: R1.Pin_1, LED1.cathode

custom parts:
  SwiftIO: SwiftIO offers a full Swift compiler and framework environment that runs on the microcontroller. The SwiftIO board is a compact electronic circuit board that runs Swift on the bare metal, giving you a system that can be used to control all kinds of electronic projects.
  SwiftIO: SwiftIO offers a full Swift compiler and framework environment that runs on the microcontroller. The SwiftIO board is a compact electronic circuit board that runs Swift on the bare metal, giving you a system that can be used to control all kinds of electronic projects.
