# Fritzing sketch PWMMelody (saved by Fritzing 0.9.3b)
breadboards: 1

parts:
  元件4 = SwiftIO  # not connected
  元件5 = SwiftIO
  J1 = Piezo Speaker

nets:
  N1: 元件5.GND, J1.pin1
  N2: 元件5.P10/D10/PWM2B, J1.pin2

custom parts:
  SwiftIO: SwiftIO offers a full Swift compiler and framework environment that runs on the microcontroller. The SwiftIO board is a compact electronic circuit board that runs Swift on the bare metal, giving you a system that can be used to control all kinds of electronic projects.
  SwiftIO: SwiftIO offers a full Swift compiler and framework environment that runs on the microcontroller. The SwiftIO board is a compact electronic circuit board that runs Swift on the bare metal, giving you a system that can be used to control all kinds of electronic projects.
