# Fritzing sketch ReadAnalogInput (saved by Fritzing 0.9.3b)
breadboards: 1

parts:
  元件1 = SwiftIO  # not connected
  元件2 = SwiftIO
  R1 = Rotary Potentiometer (Small) [maximum_resistance=100kΩ package=THT]

nets:
  N1: 元件2.P20/D20/A6, R1.wiper
  N2: 元件2.GND, R1.leg1
  N3: 元件2.3V3, R1.leg2

custom parts:
  SwiftIO: SwiftIO offers a full Swift compiler and framework environment that runs on the microcontroller. The SwiftIO board is a compact electronic circuit board that runs Swift on the bare metal, giving you a system that can be used to control all kinds of electronic projects.
  SwiftIO: SwiftIO offers a full Swift compiler and framework environment that runs on the microcontroller. The SwiftIO board is a compact electronic circuit board that runs Swift on the bare metal, giving you a system that can be used to control all kinds of electronic projects.
