# Fritzing sketch ReadDigitalInput (saved by Fritzing 0.9.3b)
breadboards: 1

parts:
  元件1 = SwiftIO  # not connected
  元件2 = SwiftIO
  S1 = Pushbutton [package="[THT]"]

nets:
  N1: 元件2.3V3, S1.Pin_3, S1.Pin_4
  N2: 元件2.P10/D10/PWM2B, S1.Pin_1, S1.Pin_2

custom parts:
  SwiftIO: SwiftIO offers a full Swift compiler and framework environment that runs on the microcontroller. The SwiftIO board is a compact electronic circuit board that runs Swift on the bare metal, giving you a system that can be used to control all kinds of electronic projects.
  SwiftIO: SwiftIO offers a full Swift compiler and framework environment that runs on the microcontroller. The SwiftIO board is a compact electronic circuit board that runs Swift on the bare metal, giving you a system that can be used to control all kinds of electronic projects.
